// Logisim project PSG.circ as structural Verilog: 2 circuits, main circuit main
module main (
  input  PSG_TEST_OE,
  input  D0,
  input  D1,
  input  D2,
  input  D3,
  input  D4,
  input  D5,
  input  D6,
  input  D7,
  input  D8,
  input  D9,
  input  D10,
  input  D11,
  input  D12,
  input  D13,
  input  D14,
  input  D15,
  output D0_2,
  output D1_2,
  output D2_2,
  output D3_2,
  output D4_2,
  output D5_2,
  output D6_2,
  output D7_2,
  output D8_2,
  output D9_2,
  output D10_2,
  output D11_2,
  output D12_2,
  output D13_2,
  output D14_2,
  output D15_2,
  output out_34,
  output out_35,
  output out_36,
  output [7:0] DAC0,
  output out_38,
  output out_39,
  output out_40,
  output [7:0] DAC1,
  output out_42,
  output out_43,
  output out_44,
  output [7:0] DAC2,
  output out_46,
  output out_47,
  output out_48,
  output [7:0] DAC3
);

  wire _67_out, _80_out, _93_out, _106_out, _111_out, _115_out, _118_out, _121_out, _124_out, _125_out,
       _128_out, _129_out, _131_out, _132_out, _134_out, _135_out, _138_2_out, _138_out, _139_out,
       _141_2_out, _141_out, _142_out, _156_2_out, _156_out, _157_out, _163_out, _164_2_out, _164_out,
       _174_out, _175_out, _176_out, _177_out, and_1_out, d_latch_1_q, d_latch_2_q, d_latch_3_q, d_latch_4_q,
       d_latch_5_q, d_latch_6_q, d_latch_7_q, d_latch_8_q, d_latch_9_q, d_latch_10_q, d_latch_11_q,
       d_latch_12_q, d_latch_13_q, d_latch_14_q, d_latch_15_q, d_latch_16_q, d_latch_17_q, d_latch_18_q,
       d_latch_19_q, d_latch_20_q, d_latch_21_q, d_latch_22_q, d_latch_23_q, d_latch_24_q, not_1_out,
       not_2_out, not_3_out, not_4_out, not_5_out, not_6_out, not_7_out, not_8_out, not_9_out, not_10_out,
       not_11_out, not_12_out, not_13_out, not_14_out, not_15_out, not_16_out, not_17_out, not_18_out,
       not_19_out, not_20_out, not_21_out, not_22_out, undriven, undriven_2, undriven_3, undriven_4,
       undriven_5, undriven_6, undriven_7, undriven_8, undriven_9, undriven_10, undriven_11;
  wire [1:0] undriven_12;
  wire [2:0] _58_out, _71_out, _84_out, _97_out;

  // AND_Gate _139 has open pins: out=_139_out
  // AND_Gate _142 has open pins: out=_142_out
  // AND_Gate _157 has open pins: out=_157_out
  // AND_Gate _163 has open pins: out=_163_out
  and _138 (_138_out, _139_out, undriven);
  and _141 (_141_out, _142_out, undriven);
  and _156 (_156_out, _157_out, undriven);
  and _164 (_164_out, _163_out, undriven);
  nor _138_2 (_138_2_out, _138_out, undriven_3);
  nor _141_2 (_141_2_out, _141_out, undriven_3);
  nor _156_2 (_156_2_out, _156_out, undriven_3);
  nor _164_2 (_164_2_out, _164_out, undriven_3);
  D_LATCH d_latch_1 (.EN(undriven_2), .D(D7), .Q(d_latch_1_q));  // open: nQ
  D_LATCH d_latch_2 (.EN(undriven_2), .D(D6), .Q(d_latch_2_q));  // open: nQ
  D_LATCH d_latch_3 (.EN(undriven_2), .D(D5), .Q(d_latch_3_q));  // open: nQ
  D_LATCH d_latch_4 (.EN(undriven_2), .D(D4), .Q(d_latch_4_q));  // open: nQ
  D_LATCH d_latch_5 (.EN(undriven_2), .D(D3), .Q(d_latch_5_q));  // open: nQ
  D_LATCH d_latch_6 (.EN(undriven_2), .D(D2), .Q(d_latch_6_q));  // open: nQ
  D_LATCH d_latch_7 (.EN(undriven_2), .D(D1), .Q(d_latch_7_q));  // open: nQ
  D_LATCH d_latch_8 (.EN(undriven_2), .D(D0), .Q(d_latch_8_q));  // open: nQ
  not not_1 (not_1_out, _138_2_out);
  not not_2 (not_2_out, _141_2_out);
  not not_3 (not_3_out, _156_2_out);
  not not_4 (not_4_out, _164_2_out);
  and _111 (_111_out, d_latch_1_q, undriven_4);
  and _115 (_115_out, d_latch_2_q, undriven_4);
  and _118 (_118_out, d_latch_3_q, undriven_4);
  and _121 (_121_out, d_latch_4_q, undriven_4);
  and _124 (_124_out, d_latch_5_q, undriven_4);
  and _128 (_128_out, d_latch_6_q, undriven_4);
  and _131 (_131_out, d_latch_7_q, undriven_4);
  and _134 (_134_out, d_latch_8_q, undriven_4);
  not not_5 (not_5_out, undriven_4);
  not not_6 (not_6_out, not_1_out);
  not not_7 (not_7_out, not_1_out);
  not not_8 (not_8_out, not_7_out);
  not not_9 (not_9_out, not_2_out);
  not not_10 (not_10_out, not_2_out);
  not not_11 (not_11_out, not_10_out);
  not not_12 (not_12_out, not_3_out);
  not not_13 (not_13_out, not_14_out);
  not not_14 (not_14_out, not_3_out);
  not not_15 (not_15_out, not_4_out);
  not not_16 (not_16_out, not_4_out);
  not not_17 (not_17_out, not_16_out);
  and and_1 (and_1_out, undriven_5, _111_out);
  or _125 (_125_out, _124_out, not_5_out);
  or _129 (_129_out, _128_out, not_5_out);
  or _132 (_132_out, _131_out, not_5_out);
  or _135 (_135_out, _134_out, not_5_out);
  D_LATCH d_latch_9 (.EN(not_8_out), .D(_125_out), .Q(d_latch_9_q));  // open: nQ
  D_LATCH d_latch_10 (.EN(not_8_out), .D(_129_out), .Q(d_latch_10_q));  // open: nQ
  D_LATCH d_latch_11 (.EN(not_8_out), .D(_132_out), .Q(d_latch_11_q));  // open: nQ
  D_LATCH d_latch_12 (.EN(not_8_out), .D(_135_out), .Q(d_latch_12_q));  // open: nQ
  D_LATCH d_latch_13 (.EN(not_11_out), .D(_125_out), .Q(d_latch_13_q));  // open: nQ
  D_LATCH d_latch_14 (.EN(not_11_out), .D(_129_out), .Q(d_latch_14_q));  // open: nQ
  D_LATCH d_latch_15 (.EN(not_11_out), .D(_132_out), .Q(d_latch_15_q));  // open: nQ
  D_LATCH d_latch_16 (.EN(not_11_out), .D(_135_out), .Q(d_latch_16_q));  // open: nQ
  D_LATCH d_latch_17 (.EN(not_13_out), .D(_125_out), .Q(d_latch_17_q));  // open: nQ
  D_LATCH d_latch_18 (.EN(not_13_out), .D(_129_out), .Q(d_latch_18_q));  // open: nQ
  D_LATCH d_latch_19 (.EN(not_13_out), .D(_132_out), .Q(d_latch_19_q));  // open: nQ
  D_LATCH d_latch_20 (.EN(not_13_out), .D(_135_out), .Q(d_latch_20_q));  // open: nQ
  D_LATCH d_latch_21 (.EN(not_17_out), .D(_125_out), .Q(d_latch_21_q));  // open: nQ
  D_LATCH d_latch_22 (.EN(not_17_out), .D(_129_out), .Q(d_latch_22_q));  // open: nQ
  D_LATCH d_latch_23 (.EN(not_17_out), .D(_132_out), .Q(d_latch_23_q));  // open: nQ
  D_LATCH d_latch_24 (.EN(not_17_out), .D(_135_out), .Q(d_latch_24_q));  // open: nQ
  nor _174 (_174_out, undriven_6, undriven_10);
  nor _175 (_175_out, undriven_7, undriven_10);
  nor _176 (_176_out, undriven_8, undriven_10);
  nor _177 (_177_out, undriven_9, undriven_10);
  or _58 (_58_out[0], d_latch_9_q, _174_out);
  or _61 (_58_out[1], d_latch_10_q, _174_out);
  or _64 (_58_out[2], d_latch_11_q, _174_out);
  or _67 (_67_out, d_latch_12_q, _174_out);
  or _71 (_71_out[0], d_latch_13_q, _175_out);
  or _74 (_71_out[1], d_latch_14_q, _175_out);
  or _77 (_71_out[2], d_latch_15_q, _175_out);
  or _80 (_80_out, d_latch_16_q, _175_out);
  or _84 (_84_out[0], d_latch_17_q, _176_out);
  or _87 (_84_out[1], d_latch_18_q, _176_out);
  or _90 (_84_out[2], d_latch_19_q, _176_out);
  or _93 (_93_out, d_latch_20_q, _176_out);
  or _97 (_97_out[0], d_latch_21_q, _177_out);
  or _100 (_97_out[1], d_latch_22_q, _177_out);
  or _103 (_97_out[2], d_latch_23_q, _177_out);
  or _106 (_106_out, d_latch_24_q, _177_out);
  not not_18 (not_18_out, out_36);
  not not_19 (not_19_out, out_40);
  not not_20 (not_20_out, out_44);
  not not_21 (not_21_out, out_48);
  not not_22 (not_22_out, PSG_TEST_OE);
  assign D0_2 = not_22_out ? ~_58_out[0] : 1'bz;  // Controlled_Inverter controlled_inverter_1
  assign D1_2 = not_22_out ? ~_58_out[1] : 1'bz;  // Controlled_Inverter controlled_inverter_2
  assign D2_2 = not_22_out ? ~_58_out[2] : 1'bz;  // Controlled_Inverter controlled_inverter_3
  assign D3_2 = not_22_out ? ~_67_out : 1'bz;  // Controlled_Inverter controlled_inverter_4
  assign D4_2 = not_22_out ? ~_71_out[0] : 1'bz;  // Controlled_Inverter controlled_inverter_5
  assign D5_2 = not_22_out ? ~_71_out[1] : 1'bz;  // Controlled_Inverter controlled_inverter_6
  assign D6_2 = not_22_out ? ~_71_out[2] : 1'bz;  // Controlled_Inverter controlled_inverter_7
  assign D7_2 = not_22_out ? ~_80_out : 1'bz;  // Controlled_Inverter controlled_inverter_8
  assign D8_2 = not_22_out ? ~_84_out[0] : 1'bz;  // Controlled_Inverter controlled_inverter_9
  assign D9_2 = not_22_out ? ~_84_out[1] : 1'bz;  // Controlled_Inverter controlled_inverter_10
  assign D10_2 = not_22_out ? ~_84_out[2] : 1'bz;  // Controlled_Inverter controlled_inverter_11
  assign D11_2 = not_22_out ? ~_93_out : 1'bz;  // Controlled_Inverter controlled_inverter_12
  assign D12_2 = not_22_out ? ~_97_out[0] : 1'bz;  // Controlled_Inverter controlled_inverter_13
  assign D13_2 = not_22_out ? ~_97_out[1] : 1'bz;  // Controlled_Inverter controlled_inverter_14
  assign D14_2 = not_22_out ? ~_97_out[2] : 1'bz;  // Controlled_Inverter controlled_inverter_15
  assign D15_2 = not_22_out ? ~_106_out : 1'bz;  // Controlled_Inverter controlled_inverter_16
  nand _3 (out_34, _106_out, not_18_out);
  nand _2 (out_35, out_34, not_18_out);
  Decoder #(.select(3), .disabled(0), .enable("false")) decoder_1 (
    .out0(DAC0[0]), .out1(DAC0[1]), .out2(DAC0[2]), .out3(DAC0[3]), .out4(DAC0[4]), .out5(DAC0[5]),
    .out6(DAC0[6]), .out7(DAC0[7]), .sel(_97_out));
  nand _17 (out_38, _93_out, not_19_out);
  nand _16 (out_39, out_38, not_19_out);
  Decoder #(.select(3), .disabled(0), .enable("false")) decoder_2 (
    .out0(DAC1[0]), .out1(DAC1[1]), .out2(DAC1[2]), .out3(DAC1[3]), .out4(DAC1[4]), .out5(DAC1[5]),
    .out6(DAC1[6]), .out7(DAC1[7]), .sel(_84_out));
  nand _31 (out_42, _80_out, not_20_out);
  nand _30 (out_43, out_42, not_20_out);
  Decoder #(.select(3), .disabled(0), .enable("false")) decoder_3 (
    .out0(DAC2[0]), .out1(DAC2[1]), .out2(DAC2[2]), .out3(DAC2[3]), .out4(DAC2[4]), .out5(DAC2[5]),
    .out6(DAC2[6]), .out7(DAC2[7]), .sel(_71_out));
  nand _45 (out_46, _67_out, not_21_out);
  nand _44 (out_47, out_46, not_21_out);
  Decoder #(.select(3), .disabled(0), .enable("false")) decoder_4 (
    .out0(DAC3[0]), .out1(DAC3[1]), .out2(DAC3[2]), .out3(DAC3[3]), .out4(DAC3[4]), .out5(DAC3[5]),
    .out6(DAC3[6]), .out7(DAC3[7]), .sel(_58_out));
  Decoder #(.select(2), .disabled(0)) decoder_5 (
    .out0(out_36), .out1(out_40), .out2(out_44), .out3(out_48), .sel(undriven_12), .en(undriven_11));

  // Notes on the sheet:
  //   110
  //   114
  //   117
  //   120
  //   123
  //   127
  //   130
  //   133
  //   137
  //   140
  //   155
  //   165
  //   126
  //   69
  //   82
  //   95
  //   108
  //   TEST9
  //   59
  //   62
  //   65
  //   68
  //   72
  //   75
  //   78
  //   81
  //   85
  //   88
  //   91
  //   94
  //   98
  //   101
  //   104
  //   107
  //   KEK3
  //   KEK2
  //   KEK1
  //   KEK0
  //   57
  //   60
  //   63
  //   66
  //   70
  //   73
  //   76
  //   79
  //   83
  //   86
  //   89
  //   92
  //   96
  //   99
  //   102
  //   105
  //   1
  //   15
  //   29
  //   43
endmodule

module D_LATCH (
  input  EN,
  input  D,
  output Q,
  output nQ
);

  D_Flip_Flop #(.trigger("high")) d_ff_1 (.clk(EN), .D(D), .Q(Q), .Qn(nQ));  // open: preset, en, reset
endmodule
